# Fritzing sketch bluscale (saved by Fritzing 0.9.3b)

parts:
  Componente1 = Arduino Pro Mini v13
  Componente2 = Bluetooth HC-05 Macho
  Componente3 = HX711 Weighing Sensor Module
  Componente7 = PowerBoost 500 Charger
  U1 = LIPO-1000mAh [package=lipo-1000]
  J1 = female pin header, 4 pins [form="♀ (female)"]
  S1 = Toggle Switch [package=THT]

nets:
  VCC: Componente1.VCC, Componente2.VCC, S1.L2
  GND: Componente1.GND, Componente2.GND, Componente3.GND, Componente7.GND
  N1: Componente1.D3_PWM, Componente3.DO/RX
  N2: Componente1.D2, Componente3.CK/TX
  N3: Componente1.D1/RX, Componente2.RXD
  N4: Componente1.D0/TX, Componente2.TXD
  N5: Componente2.State, Componente3.VCC
  N6: Componente3.E+, J1.pin4
  N7: Componente3.E-, J1.pin3
  N8: Componente3.A+, J1.pin2
  N9: Componente3.A-, J1.pin1
  N10: Componente7.GND_BAT_IN, U1.-
  N11: Componente7.VBAT_IN, U1.+
  N12: Componente7.5.0V, S1.COM

notes:
  HM-10
  SN2L1P
  loadcell
